# Fritzing sketch stacja (saved by Fritzing 0.7.5b)
breadboards: 1

parts:
  Arduino1 = Arduino
  LCD1 = LCD screen [part_number=Hitachi-like]
  U2 = mystery part, 6 pins [chip_label=? spacing=300mil]
  U1 = mystery part, 4 pins [chip_label="ranging sensor" spacing=300mil]

nets:
  GND: Arduino1.GND, LCD1.VSS, LCD1.V0, LCD1.LED+
  N1: Arduino1.D12, LCD1.RS
  N2: Arduino1.D11, LCD1.E
  N3: Arduino1.D10, U1.pin2
  N4: Arduino1.D9, U1.pin3
  N5: Arduino1.D5, LCD1.DB4
  N6: Arduino1.D4, LCD1.DB5
  N7: Arduino1.D3, LCD1.DB6
  N8: Arduino1.D2, LCD1.DB7
  N9: Arduino1.3V3, U2.pin1, U2.pin6, U1.pin1
  +5V: Arduino1.+5V, LCD1.VDD, LCD1.LED-, U1.pin4
  N10: Arduino1.A4, U2.pin2, U2.pin5
  N11: Arduino1.A5, U2.pin3, U2.pin4
